# Fritzing sketch circuts (saved by Fritzing 1.0.2b)
breadboards: 2

parts:
  Mod1 = Amica NodeMCU DEVKIT 1.0
  HLK-PM1 = HLK-PM01
  S2 = Round Pushbutton
  S3 = Round Pushbutton
  S4 = Round Pushbutton
  S5 = Round Pushbutton
  S6 = Round Pushbutton
  S7 = Round Pushbutton
  S8 = Round Pushbutton
  S9 = Round Pushbutton
  U1 = RELAY [package=relay-jzc]
  U2 = RELAY [package=relay-jzc]
  U3 = RELAY [package=relay-jzc]
  U4 = RELAY [package=relay-jzc]
  U5 = RELAY [package=relay-jzc]
  U6 = RELAY [package=relay-jzc]
  U7 = RELAY [package=relay-jzc]
  U8 = RELAY [package=relay-jzc]
  R2 = Resistor [tolerance=±5% resistance=445 package="0402 [SMD]"]
  R3 = Resistor [tolerance=±5% resistance=445 package="0402 [SMD]"]
  R4 = Resistor [tolerance=±5% resistance=445 package="0402 [SMD]"]

nets:
  N1: Mod1.pin1, Mod1.pin_10, S4.leg1, S5.leg1, S6.leg1, S7.leg1
  N2: Mod1.pin2, Mod1.pin_25, Mod1.pin_29, HLK-PM1.-Vo, S2.leg1, S3.leg1, S8.leg1, S9.leg1, U1.MAIN, U2.MAIN, U3.MAIN, U4.MAIN, U5.MAIN, U6.MAIN, U7.MAIN, U8.MAIN, R2.Pin_0, R3.Pin_0, R4.Pin_1
  N3: Mod1.pin3, S7.leg0, R4.Pin_0
  N4: Mod1.pin4, S8.leg0
  N5: Mod1.pin5, U1.COIL1
  N6: Mod1.pin6, U2.COIL1
  N7: Mod1.pin7, U3.COIL1
  N8: Mod1.pin8, U4.COIL1
  N9: Mod1.pin_11, S6.leg0, R3.Pin_1
  N10: Mod1.pin_12, S5.leg0, R2.Pin_1
  N11: Mod1.pin_13, U5.COIL1
  N12: Mod1.pin_14, U6.COIL1
  N13: Mod1.pin_15, S4.leg0
  N14: Mod1.pin_16, U7.COIL1
  N15: Mod1.pin_19, S3.leg0
  N16: Mod1.pin_20, S2.leg0
  N17: Mod1.pin_30, HLK-PM1.+Vo
